# Fritzing sketch 3_knop_if_else (saved by Fritzing 0.9.3b)
circuit board: 8.46667cm x 5.64444cm
circuit board: 8.46667cm x 5.64444cm
breadboards: 2

parts:
  L2 = LED - 5mm [color="Red (633nm)" package="5 mm [THT]"]
  A2 = Arduino Uno (Rev3)
  RL2 = Resistor [tolerance=±5% resistance=1k package=THT]
  S2 = Pushbutton [package="[THT]"]
  RS2 = Resistor [tolerance=±5% resistance=10k package=THT]
  A1 = Arduino Uno (Rev3)
  S1 = Pushbutton [package="[THT]"]
  RS1 = Resistor [tolerance=±5% resistance=10k package=THT]
  L1 = LED - 5mm [color="Red (633nm)" package="5 mm [THT]"]
  RL1 = Resistor [tolerance=±5% resistance=1k package=THT]
  L3 = LED - 5mm [color="Green (555nm)" package="5 mm [THT]"]
  RL3 = Resistor [tolerance=±5% resistance=1k package=THT]

nets:
  N1: L2.cathode, RL2.Pin_0
  N2: L2.anode, A2.D13/SCK
  N3: A2.D12/MISO, L3.anode
  N4: A2.GND, RL2.Pin_1, RS2.Pin_0, RL3.Pin_1
  N5: A2.D2, S2.Pin_1, S2.Pin_2, RS2.Pin_1
  N6: A2.5V, S2.Pin_3, S2.Pin_4
  N7: A1.D13/SCK, L1.anode
  N8: A1.GND, RS1.Pin_0, RL1.Pin_1
  N9: A1.D2, S1.Pin_1, S1.Pin_2, RS1.Pin_1
  N10: A1.5V, S1.Pin_3, S1.Pin_4
  N11: L1.cathode, RL1.Pin_0
  N12: L3.cathode, RL3.Pin_0

notes:
  1000 Ohm
  Bruin
  Zwart
  Rood
  Goud
  10000 Ohm
  Bruin
  Zwart
  Oranje
  Goud
