# Fritzing sketch 04_knop_flip (saved by Fritzing 0.9.3b)
circuit board: 8.46667cm x 5.64444cm
circuit board: 8.46667cm x 5.64444cm
circuit board: 8.46667cm x 5.64444cm
breadboards: 3

parts:
  L2 = LED - 5mm [color="Red (633nm)" package="5 mm [THT]"]
  A2 = Arduino Uno (Rev3)
  RL2 = Resistor [tolerance=±5% resistance=1k package=THT]
  S2 = Pushbutton [package="[THT]"]
  RS2 = Resistor [tolerance=±5% resistance=10k package=THT]
  A1 = Arduino Uno (Rev3)
  S1 = Pushbutton [package="[THT]"]
  RS1 = Resistor [tolerance=±5% resistance=10k package=THT]
  L1 = LED - 5mm [color="Red (633nm)" package="5 mm [THT]"]
  RL1 = Resistor [tolerance=±5% resistance=1k package=THT]
  L3 = LED - 5mm [color="Green (555nm)" package="5 mm [THT]"]
  RL3 = Resistor [tolerance=±5% resistance=1k package=THT]
  A3 = Arduino Uno (Rev3)
  S3 = Pushbutton [package="[THT]"]
  R3_S = Resistor [tolerance=±5% resistance=10k package=THT]
  L3_2 = LED - 5mm [color="Yellow (595nm)" package="5 mm [THT]"]
  L3_1 = LED - 5mm [color="Red (633nm)" package="5 mm [THT]"]
  R3_2 = Resistor [tolerance=±5% resistance=1k package=THT]
  R3_1 = Resistor [tolerance=±5% resistance=1k package=THT]
  L3_3 = LED - 5mm [color="Green (555nm)" package="5 mm [THT]"]
  R3_3 = Resistor [tolerance=±5% resistance=1k package=THT]

nets:
  N1: L2.cathode, RL2.Pin_0
  N2: L2.anode, A2.D13/SCK
  N3: A2.D12/MISO, L3.anode
  N4: A2.GND, RL2.Pin_1, RS2.Pin_0, RL3.Pin_1
  N5: A2.D2, S2.Pin_1, S2.Pin_2, RS2.Pin_1
  N6: A2.5V, S2.Pin_3, S2.Pin_4
  N7: A1.D13/SCK, L1.anode
  N8: A1.GND, RS1.Pin_0, RL1.Pin_1
  N9: A1.D2, S1.Pin_1, S1.Pin_2, RS1.Pin_1
  N10: A1.5V, S1.Pin_3, S1.Pin_4
  N11: L1.cathode, RL1.Pin_0
  N12: L3.cathode, RL3.Pin_0
  N13: A3.D11_PWM/MOSI, L3_3.anode
  N14: A3.D12/MISO, L3_2.anode
  N15: A3.D13/SCK, L3_1.anode
  N16: A3.GND, R3_S.Pin_0, R3_2.Pin_1, R3_1.Pin_1, R3_3.Pin_1
  N17: A3.D2, S3.Pin_1, S3.Pin_2, R3_S.Pin_1
  N18: A3.5V, S3.Pin_3, S3.Pin_4
  N19: L3_2.cathode, R3_2.Pin_0
  N20: L3_1.cathode, R3_1.Pin_0
  N21: L3_3.cathode, R3_3.Pin_0

notes:
  1000 Ohm
  Bruin
  Zwart
  Rood
  Goud
  10000 Ohm
  Bruin
  Zwart
  Oranje
  Goud

// code stored in the sketch: 04_knop_flip.ino
const int pin_led_rood = 13;
const int pin_led_geel = 12;
const int pin_led_groen = 11;
const int pin_knop = 2;
int welke_led_aan = 1;

void setup() 
{
  pinMode(pin_led_rood, OUTPUT);
  pinMode(pin_led_geel, OUTPUT);
  pinMode(pin_led_groen, OUTPUT);
  pinMode(pin_knop, INPUT);
}

void loop()
{
  if (digitalRead(pin_knop) == HIGH)
  {
    welke_led_aan = welke_led_aan + 1;
    if (welke_led_aan == 4)
    {
      welke_led_aan = 1;
    }
    delay(200);
  }
  
  if (welke_led_aan == 1)
  {
    digitalWrite(pin_led_rood, HIGH);
    digitalWrite(pin_led_geel, LOW);
    digitalWrite(pin_led_groen, LOW);
  }
  if (welke_led_aan == 2)
  {
    digitalWrite(pin_led_rood, LOW);
    digitalWrite(pin_led_geel, HIGH);
    digitalWrite(pin_led_groen, LOW);
  }
  if (welke_led_aan == 3)
  {
    digitalWrite(pin_led_rood, LOW);
    digitalWrite(pin_led_geel, LOW);
    digitalWrite(pin_led_groen, HIGH);
  }
}
