# Fritzing sketch 6_knop_kiest (saved by Fritzing 0.9.3b)
breadboards: 1

parts:
  A1 = Arduino Uno (Rev3)
  S2 = Pushbutton [package="[THT]"]
  RS2 = Resistor [tolerance=±5% resistance=10k package=THT]

nets:
  N1: A1.GND, RS2.Pin_0
  N2: A1.D2, S2.Pin_1, S2.Pin_2, RS2.Pin_1
  N3: A1.5V, S2.Pin_3, S2.Pin_4
